// Logisim project SixteenBitProzessor.circ as structural Verilog: 5 circuits, main circuit GatedMove
module GatedMove (
  input  I0,
  input  Enable,
  output Q0,
  output Valid
);

  wire and_2_out, nor_1_out, not_1_out, or_1_out;

  not not_1 (not_1_out, Enable);
  and and_1 (Q0, Enable, I0);
  or or_1 (or_1_out, I0, not_1_out);
  and and_2 (and_2_out, or_1_out, Q0);
  nor nor_1 (nor_1_out, Q0, or_1_out);
  or or_2 (Valid, and_2_out, nor_1_out);
endmodule

module TestGatedMove (
  input  I0_in,
  input  En_in,
  output O0,
  output Valid_out
);

  GatedMove TestGatedMove (.I0(I0_in), .Enable(En_in), .Q0(O0), .Valid(Valid_out));
endmodule

module DualRailNAND (
  input  A,
  input  B,
  input  A_En,
  input  B_En,
  output Out0,
  output OutValid
);

  wire and_1_out, nand_1_out;

  nand nand_1 (nand_1_out, A, B);
  and and_1 (and_1_out, A_En, B_En);
  GatedMove gatedmove_1 (.I0(nand_1_out), .Enable(and_1_out), .Q0(Out0), .Valid(OutValid));
endmodule

module CPU16_Regs (
  input  ExecEn,
  input  CommitEn,
  input  NPC_in0,
  input  NPC_in1,
  input  NPC_in2,
  input  NPC_in3,
  input  NPC_in4,
  input  NPC_in5,
  input  NPC_in6,
  input  NPC_in7,
  input  NPC_in8,
  input  NPC_in9,
  input  NPC_in10,
  input  NPC_in11,
  input  NPC_in12,
  input  NPC_in13,
  input  NPC_in14,
  input  NPC_in15,
  input  A_in0,
  input  A_in1,
  input  A_in2,
  input  A_in3,
  input  A_in4,
  input  A_in5,
  input  A_in6,
  input  A_in7,
  input  ADDR_in0,
  input  ADDR_in1,
  input  ADDR_in2,
  input  ADDR_in3,
  input  ADDR_in4,
  input  ADDR_in5,
  input  ADDR_in6,
  input  ADDR_in7,
  input  ADDR_in8,
  input  ADDR_in9,
  input  ADDR_in10,
  input  ADDR_in11,
  input  ADDR_in12,
  input  ADDR_in13,
  input  ADDR_in14,
  input  ADDR_in15,
  output NPC0,
  output PC0,
  output NPC1,
  output PC1,
  output NPC2,
  output PC2,
  output NPC3,
  output PC3,
  output NPC4,
  output PC4,
  output NPC5,
  output PC5,
  output NPC6,
  output PC6,
  output NPC7,
  output PC7,
  output NPC8,
  output PC8,
  output NPC9,
  output PC9,
  output NPC10,
  output PC10,
  output NPC11,
  output PC11,
  output NPC12,
  output PC12,
  output NPC13,
  output PC13,
  output NPC14,
  output PC14,
  output NPC15,
  output PC15,
  output A0,
  output A1,
  output A2,
  output A3,
  output A4,
  output A5,
  output A6,
  output A7,
  output ADDR0
);

  GatedMove gatedmove_1 (.I0(NPC_in8));  // open: Enable, Q0, Valid
  GatedMove gatedmove_2 (.I0(NPC_in9));  // open: Enable, Q0, Valid
  GatedMove gatedmove_3 (.I0(NPC_in10));  // open: Enable, Q0, Valid
  GatedMove gatedmove_4 (.I0(NPC_in12));  // open: Enable, Q0, Valid
  GatedMove gatedmove_5 (.I0(NPC_in13));  // open: Enable, Q0, Valid
  GatedMove gatedmove_6 (.I0(NPC_in14));  // open: Enable, Q0, Valid
  GatedMove gatedmove_7 (.I0(NPC_in15));  // open: Enable, Q0, Valid
endmodule

module EightGatedMove (
  input  EnIn,
  input  [7:0] In0To8,
  input  [7:0] Out0To8,
  input  EnOut
);

  wire gatedmove_1_valid, gatedmove_2_valid, gatedmove_3_valid, gatedmove_4_valid, gatedmove_5_valid,
       gatedmove_6_valid, gatedmove_7_valid, gatedmove_8_valid;

  GatedMove gatedmove_1 (.I0(In0To8[0]), .Enable(EnIn), .Q0(Out0To8[0]), .Valid(gatedmove_1_valid));
  GatedMove gatedmove_2 (.I0(In0To8[1]), .Enable(EnIn), .Q0(Out0To8[1]), .Valid(gatedmove_2_valid));
  GatedMove gatedmove_3 (.I0(In0To8[2]), .Enable(EnIn), .Q0(Out0To8[2]), .Valid(gatedmove_3_valid));
  GatedMove gatedmove_4 (.I0(In0To8[3]), .Enable(EnIn), .Q0(Out0To8[3]), .Valid(gatedmove_4_valid));
  GatedMove gatedmove_5 (.I0(In0To8[4]), .Enable(EnIn), .Q0(Out0To8[4]), .Valid(gatedmove_5_valid));
  GatedMove gatedmove_6 (.I0(In0To8[5]), .Enable(EnIn), .Q0(Out0To8[5]), .Valid(gatedmove_6_valid));
  GatedMove gatedmove_7 (.I0(In0To8[6]), .Enable(EnIn), .Q0(Out0To8[6]), .Valid(gatedmove_7_valid));
  GatedMove gatedmove_8 (.I0(In0To8[7]), .Enable(EnIn), .Q0(Out0To8[7]), .Valid(gatedmove_8_valid));
  and AOut (EnOut, gatedmove_1_valid, gatedmove_2_valid, gatedmove_3_valid, gatedmove_4_valid, gatedmove_5_valid, gatedmove_6_valid, gatedmove_7_valid, gatedmove_8_valid);
endmodule
